# Fritzing sketch scalextric (saved by Fritzing 0.6.5b)
breadboards: 1

parts:
  Arduino1 = Arduino
  VCC1 = 4 x AAA Battery Mount
  R3 = Resistor [tolerance=±5% resistance=10k package=THT]
  C2 = Tantalum Capacitor [capacitance="1 μF" voltage=16V package="100 mil [THT, tantalum]"]
  D2 = Rectifier Diode [part_number=1N4001 package="300 mil [THT]"]
  R5 = Resistor [tolerance=±5% resistance=1.5k package=THT]
  R6 = Resistor [tolerance=±5% resistance=2.2k package=THT]
  C3 = Ceramic Capacitor [capacitance=100nF package="100 mil [THT, multilayer]"]
  C4 = Tantalum Capacitor [capacitance="1 μF" package="100 mil [THT, tantalum]"]
  D3 = Rectifier Diode [part_number=1N4001 package="300 mil [THT]"]
  C5_10uF = Electrolytic Capacitor [capacitance=0.1mF voltage=16V package="100 mil [THT, electrolytic]"]
  Q1 = Basic FET P-Channel [part_number=TIP120 package="TO220 [THT]"]
  R4 = Resistor [tolerance=±5% resistance=1k package=THT]
  M1 = DC Motor
  D4 = Rectifier Diode [part_number=1N4001 package="300 mil [THT]"]
  U1 = Voltage Regulator -- 3.3 V -- LM1117
  R7 = Big Potentiometer [part_number="60 (power throttle)"]

nets:
  GND: Arduino1.GND, C2.-, R5.Pin_1, C3.0, C4.-, C5_10uF.-, Q1.source, R7.connector2
  N1: Arduino1.D9, R4.Pin_0
  N2: Arduino1.+5V, R7.connector0
  5V: Arduino1.VIN, VCC1.+, D2.cathode, C3.1, U1.connector2
  N3: Arduino1.A0, R3.Pin_0, C2.+
  N4: R3.Pin_1, R7.connector1
  3.3V: D2.anode, R6.Pin_1, C4.+, D3.cathode, M1.pin_2, D4.cathode, U1.connector1
  N5: R5.Pin_0, R6.Pin_0, D3.anode, C5_10uF.+, U1.connector0
  N6: Q1.gate, R4.Pin_1
  N7: Q1.drain, M1.pin_1, D4.anode
